# Fritzing sketch hackason_parts (saved by Fritzing 0.9.3b)

parts:
  パーツ1 = Arduino Nano (Rev3.0)  # not connected
  パーツ2 = HX711 Weighing Sensor Module
  Load_Cell1 = Load Cell - Red/white/black/green
  W1 = ESPr Developer [package="DIP (Dual Inline) [THT]"]

nets:
  N1: パーツ2.VCC, W1.VOUT
  GND: パーツ2.GND, W1.GND
  N2: パーツ2.DO/RX, W1.IO0
  N3: パーツ2.CK/TX, W1.IO2
  N4: パーツ2.E+, Load_Cell1.wire1
  N5: パーツ2.E-, Load_Cell1.wire3
  N6: パーツ2.A+, Load_Cell1.wire4
  N7: パーツ2.A-, Load_Cell1.wire2

notes:
  ロードセル
  HX711(ロードセル用ADコンバータ)
  arduino本体(バイブレーション制御に使うかも...?)

custom parts:
  Load Cell - Red/white/black/green: A rectangle load cell/weighting pressure Sensor with four wires - Red, white, black, green. Normally corresponding with E+, E-, A+, A- respectively.

// code stored in the sketch: Untitled2.ino
#include <SoftwareSerial.h>
#include <ArduinoESPAT.h>

ESPAT espat("BCW710J-05B786-A", "4a9f585ebce26");

void setup() {
  // put your setup code here, to run once:
  Serial.begin(115200);

  if (espat.begin()){
    Serial.println("Initialize OK");
  }else{
    Serial.println("Initialize Fail");
  }

  if (espat.changeMode(1)){
    Serial.println("Mode OK");
  }else{
    Serial.println("Mode not OK");
  }

  if (espat.tryConnectAP()){
    Serial.println("Connected");
  }else{
     Serial.println("Connect Failed");
  }
  Serial.println(espat.clientIP());

  Serial.println(espat.get("gihyo.jp", "/", 80));
  
}

void loop() {
  // put your main code here, to run repeatedly:

}
